// Logisim project ex1.circ as structural Verilog: 1 circuit, main circuit generate_immediate
module generate_immediate (
  input  [31:0] INSTRUCTION,
  output [31:0] IMMEDIATE
);


  assign IMMEDIATE = {{21{INSTRUCTION[31]}}, INSTRUCTION[30:25], INSTRUCTION[11:7]};

  // Other names for the same wires on the sheet: A = INSTRUCTION[31]
endmodule
