// Logisim project regfile.circ as structural Verilog: 1 circuit, main circuit regfile
module regfile (
  input  [4:0] ReadReg1,
  input  [4:0] ReadReg2,
  input  [4:0] WriteReg,
  input  [31:0] RegWriteData,
  input  RegWEn,
  input  clk,
  output [31:0] ra,
  output [31:0] sp,
  output [31:0] t0,
  output [31:0] t1,
  output [31:0] t2,
  output [31:0] s0,
  output [31:0] s1,
  output [31:0] a0,
  output [31:0] RegReadData1,
  output [31:0] RegReadData2
);

  wire and_1_out, and_2_out, and_3_out, and_4_out, and_5_out, and_6_out, and_7_out, and_8_out, and_9_out,
       and_10_out, and_11_out, and_12_out, and_13_out, and_14_out, and_15_out, and_16_out, and_17_out,
       and_18_out, and_19_out, and_20_out, and_21_out, and_22_out, and_23_out, and_24_out, and_25_out,
       and_26_out, and_27_out, and_28_out, and_29_out, and_30_out, and_31_out, and_32_out, w00, w01, w02,
       w03, w04, w05, w06, w07, w08, w09, w10, w11, w12, w13, w14, w15, w16, w17, w18, w19, w20, w21, w22,
       w23, w24, w25, w26, w27, w28, w29, w30, w31;
  wire [31:0] r00, r03, r04, r11, r12, r13, r14, r15, r16, r17, r18, r19, r20, r21, r22, r23, r24, r25, r26,
       r27, r28, r29, r30, r31;

  Register #(.width(32)) register_1 (.D({32{1'b0}}), .en(and_1_out), .clk(clk), .Q(r00));  // open: clr
  and and_1 (and_1_out, RegWEn, w00);
  Register #(.width(32)) register_2 (.D(RegWriteData), .en(and_2_out), .clk(clk), .Q(ra));  // open: clr
  and and_2 (and_2_out, RegWEn, w01);
  Register #(.width(32)) register_3 (.D(RegWriteData), .en(and_3_out), .clk(clk), .Q(sp));  // open: clr
  and and_3 (and_3_out, RegWEn, w02);
  Register #(.width(32)) register_4 (.D(RegWriteData), .en(and_4_out), .clk(clk), .Q(r03));  // open: clr
  and and_4 (and_4_out, RegWEn, w03);
  Register #(.width(32)) register_5 (.D(RegWriteData), .en(and_5_out), .clk(clk), .Q(r04));  // open: clr
  and and_5 (and_5_out, RegWEn, w04);
  Register #(.width(32)) register_6 (.D(RegWriteData), .en(and_6_out), .clk(clk), .Q(t0));  // open: clr
  and and_6 (and_6_out, RegWEn, w05);
  Register #(.width(32)) register_7 (.D(RegWriteData), .en(and_7_out), .clk(clk), .Q(t1));  // open: clr
  and and_7 (and_7_out, RegWEn, w06);
  Register #(.width(32)) register_8 (.D(RegWriteData), .en(and_8_out), .clk(clk), .Q(t2));  // open: clr
  and and_8 (and_8_out, RegWEn, w07);
  Register #(.width(32)) register_9 (.D(RegWriteData), .en(and_9_out), .clk(clk), .Q(s0));  // open: clr
  and and_9 (and_9_out, RegWEn, w08);
  Register #(.width(32)) register_10 (.D(RegWriteData), .en(and_10_out), .clk(clk), .Q(s1));  // open: clr
  and and_10 (and_10_out, RegWEn, w09);
  Register #(.width(32)) register_11 (.D(RegWriteData), .en(and_11_out), .clk(clk), .Q(a0));  // open: clr
  and and_11 (and_11_out, RegWEn, w10);
  Register #(.width(32)) register_12 (.D(RegWriteData), .en(and_12_out), .clk(clk), .Q(r11));  // open: clr
  and and_12 (and_12_out, RegWEn, w11);
  Register #(.width(32)) register_13 (.D(RegWriteData), .en(and_13_out), .clk(clk), .Q(r12));  // open: clr
  and and_13 (and_13_out, RegWEn, w12);
  Register #(.width(32)) register_14 (.D(RegWriteData), .en(and_14_out), .clk(clk), .Q(r13));  // open: clr
  and and_14 (and_14_out, RegWEn, w13);
  Register #(.width(32)) register_15 (.D(RegWriteData), .en(and_15_out), .clk(clk), .Q(r14));  // open: clr
  and and_15 (and_15_out, RegWEn, w14);
  Register #(.width(32)) register_16 (.D(RegWriteData), .en(and_16_out), .clk(clk), .Q(r15));  // open: clr
  and and_16 (and_16_out, RegWEn, w15);
  Register #(.width(32)) register_17 (.D(RegWriteData), .en(and_17_out), .clk(clk), .Q(r16));  // open: clr
  and and_17 (and_17_out, RegWEn, w16);
  Register #(.width(32)) register_18 (.D(RegWriteData), .en(and_18_out), .clk(clk), .Q(r17));  // open: clr
  and and_18 (and_18_out, RegWEn, w17);
  Register #(.width(32)) register_19 (.D(RegWriteData), .en(and_19_out), .clk(clk), .Q(r18));  // open: clr
  and and_19 (and_19_out, RegWEn, w18);
  Register #(.width(32)) register_20 (.D(RegWriteData), .en(and_20_out), .clk(clk), .Q(r19));  // open: clr
  and and_20 (and_20_out, RegWEn, w19);
  and and_21 (and_21_out, RegWEn, w20);
  and and_22 (and_22_out, RegWEn, w21);
  and and_23 (and_23_out, RegWEn, w22);
  and and_24 (and_24_out, RegWEn, w23);
  and and_25 (and_25_out, RegWEn, w24);
  and and_26 (and_26_out, RegWEn, w25);
  and and_27 (and_27_out, RegWEn, w26);
  and and_28 (and_28_out, RegWEn, w27);
  and and_29 (and_29_out, RegWEn, w28);
  and and_30 (and_30_out, RegWEn, w29);
  and and_31 (and_31_out, RegWEn, w30);
  and and_32 (and_32_out, RegWEn, w31);
  Register #(.width(32)) register_21 (.D(RegWriteData), .en(and_21_out), .clk(clk), .Q(r20));  // open: clr
  Register #(.width(32)) register_22 (.D(RegWriteData), .en(and_22_out), .clk(clk), .Q(r21));  // open: clr
  Register #(.width(32)) register_23 (.D(RegWriteData), .en(and_23_out), .clk(clk), .Q(r22));  // open: clr
  Register #(.width(32)) register_24 (.D(RegWriteData), .en(and_24_out), .clk(clk), .Q(r23));  // open: clr
  Register #(.width(32)) register_25 (.D(RegWriteData), .en(and_25_out), .clk(clk), .Q(r24));  // open: clr
  Register #(.width(32)) register_26 (.D(RegWriteData), .en(and_26_out), .clk(clk), .Q(r25));  // open: clr
  Register #(.width(32)) register_27 (.D(RegWriteData), .en(and_27_out), .clk(clk), .Q(r26));  // open: clr
  Register #(.width(32)) register_28 (.D(RegWriteData), .en(and_28_out), .clk(clk), .Q(r27));  // open: clr
  Register #(.width(32)) register_29 (.D(RegWriteData), .en(and_29_out), .clk(clk), .Q(r28));  // open: clr
  Register #(.width(32)) register_30 (.D(RegWriteData), .en(and_30_out), .clk(clk), .Q(r29));  // open: clr
  Register #(.width(32)) register_31 (.D(RegWriteData), .en(and_31_out), .clk(clk), .Q(r30));  // open: clr
  Register #(.width(32)) register_32 (.D(RegWriteData), .en(and_32_out), .clk(clk), .Q(r31));  // open: clr
  Decoder #(.select(5)) decoder_1 (
    .out0(w00), .out1(w01), .out2(w02), .out3(w03), .out4(w04), .out5(w05), .out6(w06), .out7(w07),
    .out8(w08), .out9(w09), .out10(w10), .out11(w11), .out12(w12), .out13(w13), .out14(w14), .out15(w15),
    .out16(w16), .out17(w17), .out18(w18), .out19(w19), .out20(w20), .out21(w21), .out22(w22), .out23(w23),
    .out24(w24), .out25(w25), .out26(w26), .out27(w27), .out28(w28), .out29(w29), .out30(w30), .out31(w31),
    .sel(WriteReg));  // open: en
  Multiplexer #(.enable("false"), .select(5), .width(32)) multiplexer_1 (
    .in0(r00), .in1(ra), .in2(sp), .in3(r03), .in4(r04), .in5(t0), .in6(t1), .in7(t2), .in8(s0), .in9(s1),
    .in10(a0), .in11(r11), .in12(r12), .in13(r13), .in14(r14), .in15(r15), .in16(r16), .in17(r17),
    .in18(r18), .in19(r19), .in20(r20), .in21(r21), .in22(r22), .in23(r23), .in24(r24), .in25(r25),
    .in26(r26), .in27(r27), .in28(r28), .in29(r29), .in30(r30), .in31(r31), .out(RegReadData1), .sel(ReadReg1));
  Multiplexer #(.enable("false"), .select(5), .width(32)) multiplexer_2 (
    .in0(r00), .in1(ra), .in2(sp), .in3(r03), .in4(r04), .in5(t0), .in6(t1), .in7(t2), .in8(s0), .in9(s1),
    .in10(a0), .in11(r11), .in12(r12), .in13(r13), .in14(r14), .in15(r15), .in16(r16), .in17(r17),
    .in18(r18), .in19(r19), .in20(r20), .in21(r21), .in22(r22), .in23(r23), .in24(r24), .in25(r25),
    .in26(r26), .in27(r27), .in28(r28), .in29(r29), .in30(r30), .in31(r31), .out(RegReadData2), .sel(ReadReg2));

  // Other names for the same wires on the sheet: r01[31:0] = ra; r02[31:0] = sp; r05[31:0] = t0; r06[31:0] = t1;
  //   r07[31:0] = t2; r08[31:0] = s0; r09[31:0] = s1; r10[31:0] = a0

  // Notes on the sheet:
  //   INPUTS to your circuit
  //   DON'T CHANGE THE LOCATIONS OF THE INPUTS AND OUTPUTS!
  //   These are DEBUG/TEST outputs from your circuit.
  //   OUTPUTS from your circuit
endmodule
